// Logisim project 1.circ as structural Verilog: 1 circuit, main circuit main
module main (
);

  wire button_1_out, button_2_out, button_3_out, button_4_out, button_5_out, button_6_out, transistor_1_out,
       transistor_2_out, transistor_3_out, transistor_4_out, transistor_5_out, transistor_6_out,
       transistor_8_out, transistor_9_out, transistor_11_out, transistor_12_out, transistor_13_out,
       transistor_14_out, transistor_15_out, transistor_16_out, transistor_17_out, transistor_18_out,
       transistor_19_out, transistor_21_out, transistor_23_out, transistor_25_out, transistor_26_out,
       transistor_27_out, transistor_29_out, transistor_30_out, transistor_31_out, transistor_32_out,
       transistor_33_out, transistor_34_out, transistor_35_out, transistor_36_out, transistor_37_out,
       transistor_38_out, transistor_39_out;

  Transistor #(.gate("br")) transistor_1 (.in(transistor_2_out), .out(transistor_1_out), .gate(button_1_out));
  Transistor #(.gate("br")) transistor_2 (.in(transistor_3_out), .out(transistor_2_out), .gate(button_1_out));
  Transistor #(.\type ("n"), .gate("br")) transistor_3 (
    .in(transistor_4_out), .out(transistor_3_out), .gate(button_1_out));
  Transistor #(.\type ("n"), .gate("br")) transistor_4 (.in(1'b1), .out(transistor_4_out), .gate(button_1_out));
  Button button_1 (.out(button_1_out));
  Transistor #(.gate("br")) transistor_5 (.in(1'b1), .out(transistor_5_out), .gate(button_1_out));
  Transistor #(.\type ("n"), .gate("br")) transistor_6 (
    .in(transistor_5_out), .out(transistor_6_out), .gate(transistor_9_out));
  Transistor #(.gate("br")) transistor_7 (.in(transistor_8_out), .out(transistor_1_out), .gate(transistor_16_out));
  Transistor transistor_8 (.in(transistor_9_out), .out(transistor_8_out), .gate(transistor_15_out));
  Transistor #(.\type ("n")) transistor_9 (.in(transistor_12_out), .out(transistor_9_out), .gate(transistor_15_out));
  Transistor #(.\type ("n"), .gate("br")) transistor_10 (
    .in(transistor_11_out), .out(transistor_9_out), .gate(transistor_16_out));
  Transistor #(.gate("br")) transistor_11 (.in(transistor_13_out), .out(transistor_11_out), .gate(button_2_out));
  Transistor #(.\type ("n")) transistor_12 (.in(transistor_14_out), .out(transistor_12_out), .gate(button_2_out));
  Transistor #(.\type ("n"), .gate("br")) transistor_13 (
    .in(transistor_16_out), .out(transistor_13_out), .gate(button_3_out));
  Transistor transistor_14 (.in(transistor_15_out), .out(transistor_14_out), .gate(button_3_out));
  Transistor transistor_15 (.in(transistor_18_out), .out(transistor_15_out), .gate(button_2_out));
  Transistor #(.\type ("n"), .gate("br")) transistor_16 (
    .in(transistor_17_out), .out(transistor_16_out), .gate(button_2_out));
  Transistor #(.gate("br")) transistor_17 (.in(1'b1), .out(transistor_17_out), .gate(button_3_out));
  Transistor #(.\type ("n")) transistor_18 (.in(1'b1), .out(transistor_18_out), .gate(button_3_out));
  Button button_2 (.out(button_2_out));
  Button button_3 (.out(button_3_out));
  Transistor #(.\type ("n"), .gate("br")) transistor_19 (
    .in(transistor_6_out), .out(transistor_19_out), .gate(button_1_out));
  Transistor #(.gate("br")) transistor_20 (.in(transistor_19_out), .out(transistor_1_out), .gate(transistor_9_out));
  Transistor #(.\type ("n")) transistor_21 (.in(1'b1), .out(transistor_21_out), .gate(transistor_6_out));
  Transistor #(.\type ("n"), .gate("br")) transistor_22 (.in(1'b1), .out(transistor_21_out), .gate(transistor_3_out));
  LED led_1 (.in(transistor_21_out));
  Transistor #(.gate("br")) transistor_23 (.in(transistor_21_out), .out(transistor_23_out), .gate(transistor_3_out));
  Transistor transistor_24 (.in(transistor_23_out), .out(transistor_1_out), .gate(transistor_6_out));
  Transistor #(.gate("br")) transistor_25 (.in(transistor_26_out), .out(transistor_25_out), .gate(transistor_33_out));
  Transistor transistor_26 (.in(transistor_27_out), .out(transistor_26_out), .gate(transistor_34_out));
  LED led_2 (.in(transistor_27_out));
  Transistor #(.\type ("n"), .gate("br")) transistor_27 (
    .in(transistor_29_out), .out(transistor_27_out), .gate(transistor_33_out));
  Transistor #(.\type ("n")) transistor_28 (.in(transistor_30_out), .out(transistor_27_out), .gate(transistor_34_out));
  Transistor #(.gate("br")) transistor_29 (.in(transistor_32_out), .out(transistor_29_out), .gate(button_4_out));
  Transistor #(.\type ("n")) transistor_30 (.in(transistor_31_out), .out(transistor_30_out), .gate(button_4_out));
  Transistor transistor_31 (.in(transistor_34_out), .out(transistor_31_out), .gate(1'b1));
  Transistor #(.\type ("n"), .gate("br")) transistor_32 (.in(transistor_33_out), .out(transistor_32_out), .gate(1'b1));
  Transistor #(.\type ("n"), .gate("br")) transistor_33 (
    .in(transistor_36_out), .out(transistor_33_out), .gate(button_4_out));
  Transistor transistor_34 (.in(transistor_35_out), .out(transistor_34_out), .gate(button_4_out));
  Transistor #(.\type ("n")) transistor_35 (.in(1'b1), .out(transistor_35_out), .gate(1'b1));
  Transistor #(.gate("br")) transistor_36 (.in(1'b1), .out(transistor_36_out), .gate(1'b1));
  Button button_4 (.out(button_4_out));
  Button button_5 (.out(button_5_out));
  Transistor #(.\type ("n")) transistor_37 (.in(1'b1), .out(transistor_37_out), .gate(button_5_out));
  Transistor #(.gate("br")) transistor_38 (.in(transistor_37_out), .out(transistor_38_out), .gate(button_6_out));
  Transistor transistor_39 (.in(transistor_38_out), .out(transistor_39_out), .gate(button_5_out));
  Button button_6 (.out(button_6_out));
  Transistor #(.\type ("n"), .gate("br")) transistor_40 (.in(1'b1), .out(transistor_37_out), .gate(button_6_out));
  LED led_3 (.in(transistor_37_out));
  // also tied to GND on the sheet: {transistor_1_out, transistor_25_out, transistor_39_out}

  // Notes on the sheet:
  //   A        B                       C        D
endmodule
