// Logisim project CPU.circ as structural Verilog: 5 circuits, main circuit main
module main (
);

  wire and_1_out, and_2_out, and_3_out, button_1_out, cmp_output, decoder_1_out0, decoder_1_out1,
       multiplexer_1_out, not_1_out, program_logic_1_arith_in, program_logic_1_compare,
       program_logic_1_reg1_read_en, program_logic_1_reg2_read_en, program_logic_1_reg_bank_sel,
       program_logic_1_reg_write_en, Reset_out;
  wire [1:0] multiplexer_3_out, program_logic_1_arith_fn_sel, program_logic_1_reg1_sel,
       program_logic_1_reg2_sel;
  wire [3:0] arithmics_1__4_bit_output, arithmics_2__4_bit_output, multiplexer_2_out, multiplexer_4_out,
       multiplexer_5_out, multiplexer_6_out, multiplexer_7_out, program_logic_1_output1,
       register_bank_1_arithmatic_value, register_bank_1_reg1_output, register_bank_1_reg2_output,
       register_bank_2_arithmatic_value, register_bank_2_reg1_output, register_bank_2_reg2_output;

  and and_1 (and_1_out, program_logic_1_reg_write_en, decoder_1_out0);
  and and_2 (and_2_out, program_logic_1_reg_write_en, decoder_1_out1);
  and and_3 (and_3_out, program_logic_1_reg_write_en, decoder_1_out1);
  Program_Logic program_logic_1 (
    .clock(button_1_out), .reset(Reset_out), .Output1(program_logic_1_output1),
    .Reg2_Sel(program_logic_1_reg2_sel), .Reg1_Sel(program_logic_1_reg1_sel),
    .Reg2_Read_En(program_logic_1_reg2_read_en), .Reg1_Read_En(program_logic_1_reg1_read_en),
    .Reg_Write_En(program_logic_1_reg_write_en), .Compare(program_logic_1_compare),
    .Jmp_Fnct_Sel(cmp_output), .Jmp_En(cmp_output), .Reg_Input_1(multiplexer_5_out),
    .Reg_Input_2(multiplexer_6_out), .Reg_Bank_Sel(program_logic_1_reg_bank_sel),
    .Arith_Fn_Sel(program_logic_1_arith_fn_sel), .Arith_In(program_logic_1_arith_in));  // open: Output2
  Button button_1 (.out(button_1_out));
  Button Reset (.out(Reset_out));
  Decoder #(.enable("false")) decoder_1 (
    .out0(decoder_1_out0), .out1(decoder_1_out1), .sel(program_logic_1_reg_bank_sel));
  Register_Bank register_bank_1 (
    .reset(Reset_out), .Write_Select(program_logic_1_reg1_sel), .Write_Enable(and_1_out),
    .Input(program_logic_1_output1), .Reg1_Output(register_bank_1_reg1_output),
    .Read_Reg1_En(program_logic_1_reg1_read_en), .Read_Reg1_Sel(program_logic_1_reg1_sel),
    .Reg2_Output(register_bank_1_reg2_output), .Read_Reg2_En(program_logic_1_reg2_read_en),
    .Read_Reg2_Sel(program_logic_1_reg2_sel), .Arithmatic_Value(register_bank_1_arithmatic_value),
    .Arith_Fn_Sel(program_logic_1_arith_fn_sel));  // open: Reg_11, Reg_10, Reg_01, Reg_00
  not not_1 (not_1_out, and_2_out);
  Register_Bank register_bank_2 (
    .reset(Reset_out), .Write_Select(multiplexer_3_out), .Write_Enable(multiplexer_1_out),
    .Input(multiplexer_2_out), .Reg1_Output(register_bank_2_reg1_output),
    .Read_Reg1_En(program_logic_1_reg1_read_en), .Read_Reg1_Sel(program_logic_1_reg1_sel),
    .Reg2_Output(register_bank_2_reg2_output), .Read_Reg2_En(program_logic_1_reg2_read_en),
    .Read_Reg2_Sel(program_logic_1_reg2_sel), .Arithmatic_Value(register_bank_2_arithmatic_value),
    .Arith_Fn_Sel(program_logic_1_arith_fn_sel));  // open: Reg_11, Reg_10, Reg_01, Reg_00
  Multiplexer #(.enable("false")) multiplexer_1 (.in0(and_3_out), .in1(1'b1), .out(multiplexer_1_out), .sel(not_1_out));
  Multiplexer #(.width(4), .enable("false")) multiplexer_2 (
    .in0(program_logic_1_output1), .in1(register_bank_1_arithmatic_value), .out(multiplexer_2_out),
    .sel(not_1_out));
  Multiplexer #(.width(2), .enable("false")) multiplexer_3 (
    .in0(program_logic_1_reg1_sel), .in1(2'b11), .out(multiplexer_3_out), .sel(not_1_out));
  cmp cmp (.En(program_logic_1_compare), .Input_1(multiplexer_5_out), .Input_2(multiplexer_6_out), .Output(cmp_output));
  Multiplexer #(.width(4), .enable("false")) multiplexer_4 (
    .in0(register_bank_1_reg1_output), .in1(register_bank_2_reg1_output), .out(multiplexer_4_out),
    .sel(program_logic_1_reg_bank_sel));
  Multiplexer #(.width(4), .disabled(0), .enable("false")) multiplexer_5 (
    .in0(multiplexer_4_out), .in1(multiplexer_7_out), .out(multiplexer_5_out), .sel(program_logic_1_arith_in));
  Multiplexer #(.width(4), .enable("false")) multiplexer_6 (
    .in0(register_bank_1_reg2_output), .in1(register_bank_2_reg2_output), .out(multiplexer_6_out),
    .sel(program_logic_1_reg_bank_sel));
  Multiplexer #(.width(4), .enable("false")) multiplexer_7 (
    .in0(arithmics_1__4_bit_output), .in1(arithmics_2__4_bit_output), .out(multiplexer_7_out),
    .sel(program_logic_1_reg_bank_sel));
  Arithmics arithmics_1 (
    .Function_Select(program_logic_1_arith_fn_sel), ._4_Bit_Output(arithmics_1__4_bit_output),
    ._4_Bit_Input_1(register_bank_1_reg1_output), ._4_Bit_Input_2(register_bank_1_reg2_output));  // open: Input_1, Input_2, _8_Bit_Output
  Arithmics arithmics_2 (
    .Function_Select(program_logic_1_arith_fn_sel), ._4_Bit_Output(arithmics_2__4_bit_output),
    ._4_Bit_Input_1(register_bank_2_reg1_output), ._4_Bit_Input_2(register_bank_2_arithmatic_value));  // open: Input_1, Input_2, _8_Bit_Output
  // Probe on register_bank_1_reg1_output
  // Probe on register_bank_1_reg2_output
  // Probe on register_bank_1_arithmatic_value
  // Probe on register_bank_2_reg1_output
  // Probe on register_bank_2_reg2_output
  // Probe on register_bank_2_arithmatic_value

  // Notes on the sheet:
  //   Program Logic
  //   Register Bank 1
  //   Register Bank 2
endmodule

module Program_Logic (
  input  [3:0] Reg_Input_1,
  input  [3:0] Reg_Input_2,
  input  clock,
  input  reset,
  input  Jmp_En,
  input  Jmp_Fnct_Sel,
  output [3:0] Output2,
  output [3:0] Output1,
  output [1:0] Reg2_Sel,
  output [1:0] Reg1_Sel,
  output [1:0] Arith_Fn_Sel,
  output Arith_In,
  output Reg_Bank_Sel,
  output Reg2_Read_En,
  output Reg1_Read_En,
  output Reg_Write_En,
  output Compare
);

  wire or_1_out;
  wire [0:0] or_2_out;
  wire [7:0] arithmics_1__8_bit_output, multiplexer_1_out, register_1_q;
  wire [23:0] rom_1_data;

  Multiplexer #(.width(8), .enable("false")) multiplexer_1 (
    .in0(8'h1), .in1({4'b0000, Output1}), .out(multiplexer_1_out), .sel(or_1_out));
  or or_1 (or_1_out, Jmp_En, rom_1_data[23]);
  Arithmics arithmics_1 (
    .Input_1(register_1_q), .Input_2(multiplexer_1_out), .Function_Select({1'b0, or_2_out[0]}),
    ._8_Bit_Output(arithmics_1__8_bit_output));  // open: _4_Bit_Output, _4_Bit_Input_1, _4_Bit_Input_2
  // Probe on arithmics_1__8_bit_output
  Register register_1 (.D(arithmics_1__8_bit_output), .Q(register_1_q), .clk(clock), .clr(reset));  // open: en
  or or_2 (or_2_out[0], rom_1_data[22], Jmp_Fnct_Sel);
  Multiplexer #(.width(4), .disabled(0), .enable("false")) multiplexer_2 (
    .in0(rom_1_data[7:4]), .in1(Reg_Input_1), .out(Output1), .sel(rom_1_data[13]));
  ROM #(.dataWidth(24)) rom_1 (
    .addr(register_1_q),
    .data({rom_1_data[23:22], Compare, Reg_Write_En, Reg1_Read_En, Reg2_Read_En, Reg_Bank_Sel, Arith_In, Arith_Fn_Sel, rom_1_data[13:12], Reg1_Sel, Reg2_Sel, rom_1_data[7:0]}));  // open: sel
  Multiplexer #(.width(4), .disabled(0), .enable("false")) multiplexer_3 (
    .in0(rom_1_data[3:0]), .in1(Reg_Input_2), .out(Output2), .sel(rom_1_data[12]));

  // Notes on the sheet:
  //   contents of rom_1 (hex, n*v repeats v):
  //   c0000 1c0c60 1c0410 1c0810 1c0000 d2100 100000 d2900
endmodule

module Register_Bank (
  input  [1:0] Arith_Fn_Sel,
  input  [1:0] Write_Select,
  input  Write_Enable,
  input  Read_Reg1_En,
  input  [1:0] Read_Reg1_Sel,
  input  Read_Reg2_En,
  input  [3:0] Input,
  input  reset,
  input  [1:0] Read_Reg2_Sel,
  output [3:0] Arithmatic_Value,
  output [3:0] Reg1_Output,
  output [3:0] Reg_11,
  output [3:0] Reg_10,
  output [3:0] Reg_01,
  output [3:0] Reg_00,
  output [3:0] Reg2_Output
);

  wire decoder_1_out0, decoder_1_out1, decoder_1_out2, decoder_1_out3, not_1_out, not_2_out, not_3_out,
       not_4_out;

  Decoder #(.select(2), .disabled(0)) decoder_1 (
    .out0(decoder_1_out0), .out1(decoder_1_out1), .out2(decoder_1_out2), .out3(decoder_1_out3),
    .sel(Write_Select), .en(Write_Enable));
  not not_1 (not_1_out, decoder_1_out3);
  Register #(.width(4)) register_1 (.D(Input), .en(not_1_out), .Q(Reg_11), .clk(decoder_1_out3), .clr(reset));
  Register #(.width(4)) register_2 (.D(Input), .en(not_2_out), .Q(Reg_10), .clk(decoder_1_out2), .clr(reset));
  not not_2 (not_2_out, decoder_1_out2);
  not not_3 (not_3_out, decoder_1_out1);
  Arithmics arithmics_1 (
    .Function_Select(Arith_Fn_Sel), ._4_Bit_Output(Arithmatic_Value), ._4_Bit_Input_1(Reg_01),
    ._4_Bit_Input_2(Reg_00));  // open: Input_1, Input_2, _8_Bit_Output
  Register #(.width(4)) register_3 (.D(Input), .en(not_3_out), .Q(Reg_01), .clk(decoder_1_out1), .clr(reset));
  Register #(.width(4)) register_4 (.D(Input), .en(not_4_out), .Q(Reg_00), .clk(decoder_1_out0), .clr(reset));
  not not_4 (not_4_out, decoder_1_out0);
  Multiplexer #(.select(2), .width(4)) multiplexer_1 (
    .in0(Reg_00), .in1(Reg_01), .in2(Reg_10), .in3(Reg_11), .out(Reg1_Output), .sel(Read_Reg1_Sel),
    .en(Read_Reg1_En));
  Multiplexer #(.select(2), .width(4)) multiplexer_2 (
    .in0(Reg_00), .in1(Reg_01), .in2(Reg_10), .in3(Reg_11), .out(Reg2_Output), .sel(Read_Reg2_Sel),
    .en(Read_Reg2_En));
endmodule

module Arithmics (
  input  [7:0] Input_1,
  input  [7:0] Input_2,
  input  [1:0] Function_Select,
  input  [3:0] _4_Bit_Input_1,
  input  [3:0] _4_Bit_Input_2,
  output [7:0] _8_Bit_Output,
  output [3:0] _4_Bit_Output
);

  wire [3:0] adder_2_out, divider_2_out, multiplier_2_out, subtractor_2_out;
  wire [7:0] adder_1_out, divider_1_out, multiplier_1_out, subtractor_1_out;

  Adder adder_1 (.a(Input_1), .b(Input_2), .out(adder_1_out));  // open: cin, cout
  Subtractor subtractor_1 (.a(Input_1), .b(Input_2), .out(subtractor_1_out));  // open: bin, bout
  Multiplier multiplier_1 (.a(Input_1), .b(Input_2), .out(multiplier_1_out));  // open: cin, cout
  Divider divider_1 (.a(Input_1), .b(Input_2), .out(divider_1_out));  // open: upper, rem
  Adder #(.width(4)) adder_2 (.a(_4_Bit_Input_1), .b(_4_Bit_Input_2), .out(adder_2_out));  // open: cin, cout
  Subtractor #(.width(4)) subtractor_2 (
    .a(_4_Bit_Input_1), .b(_4_Bit_Input_2), .out(subtractor_2_out));  // open: bin, bout
  Multiplier #(.width(4)) multiplier_2 (
    .a(_4_Bit_Input_1), .b(_4_Bit_Input_2), .out(multiplier_2_out));  // open: cin, cout
  Divider #(.width(4)) divider_2 (.a(_4_Bit_Input_1), .b(_4_Bit_Input_2), .out(divider_2_out));  // open: upper, rem
  Multiplexer #(.select(2), .width(8), .enable("false")) multiplexer_1 (
    .in0(adder_1_out), .in1(subtractor_1_out), .in2(multiplier_1_out), .in3(divider_1_out),
    .out(_8_Bit_Output), .sel(Function_Select));
  Multiplexer #(.select(2), .width(4), .enable("false")) multiplexer_2 (
    .in0(adder_2_out), .in1(subtractor_2_out), .in2(multiplier_2_out), .in3(divider_2_out),
    .out(_4_Bit_Output), .sel(Function_Select));
endmodule

module cmp (
  input  En,
  input  [3:0] Input_1,
  input  [3:0] Input_2,
  output Output
);

  wire comparator_1_eq, comparator_1_gt, or_1_out;

  Comparator #(.width(4)) comparator_1 (
    .a(Input_1), .b(Input_2), .gt(comparator_1_gt), .eq(comparator_1_eq));  // open: lt
  Multiplexer #(.disabled(0), .enable("false")) multiplexer_1 (.in0(1'b0), .in1(or_1_out), .out(Output), .sel(En));
  or or_1 (or_1_out, comparator_1_gt, comparator_1_eq);
endmodule
