// Logisim project CPU2.circ as structural Verilog
module Register_Bank (
  input  [7:0] Output,
  input  [1:0] Read_Select,
  input  [7:0] Input,
  input  Reset,
  input  [1:0] Write_Select,
  input  Write_Enable
);

  wire decoder_1_out0, decoder_1_out1, decoder_1_out2, decoder_1_out3, not_1_out, not_2_out, not_3_out,
       not_4_out;
  wire [7:0] register_1_q, register_2_q, register_3_q, register_4_q;

  not not_1 (not_1_out, decoder_1_out0);
  Register register_1 (.D(Input), .en(not_1_out), .Q(register_1_q), .clk(decoder_1_out0), .clr(Reset));
  not not_2 (not_2_out, decoder_1_out1);
  Multiplexer #(.select(2), .width(8), .enable("false")) multiplexer_1 (
    .in0(register_1_q), .in1(register_2_q), .in2(register_3_q), .in3(register_4_q), .out(Output),
    .sel(Read_Select));
  Register register_2 (.D(Input), .en(not_2_out), .Q(register_2_q), .clk(decoder_1_out1), .clr(Reset));
  Decoder #(.select(2)) decoder_1 (
    .out0(decoder_1_out0), .out1(decoder_1_out1), .out2(decoder_1_out2), .out3(decoder_1_out3),
    .sel(Write_Select), .en(Write_Enable));
  Register register_3 (.D(Input), .en(not_3_out), .Q(register_3_q), .clk(decoder_1_out2), .clr(Reset));
  not not_3 (not_3_out, decoder_1_out2);
  Register register_4 (.D(Input), .en(not_4_out), .Q(register_4_q), .clk(decoder_1_out3), .clr(Reset));
  not not_4 (not_4_out, decoder_1_out3);
endmodule

module Program_ROM (
);

  wire [7:0] register_1_q;

  Register register_1 (.Q(register_1_q));  // open: D, en, clk, clr
  ROM #(.dataWidth(24)) rom_1 (.addr(register_1_q));  // open: data, sel
endmodule
